// Logisim project processor.circ as structural Verilog: 2 circuits, main circuit main
// ALU_B_MUX
module main (
  input  in_1,
  input  Reset
);

  wire ALUSrc, and_1_out, and_2_out, BranchEQ, BranchNE, clock_1_out, clock_2_out, clock_3_out,
       decoder_1_out0, decoder_1_out1, decoder_1_out2, decoder_1_out3, decoder_1_out4, decoder_1_out5,
       decoder_1_out6, decoder_1_out7, MemRead, MemToReg, MemWrite, not_1_out, or_1_out, RegWrite, Zero;
  wire [1:0] ALUOp;
  wire [2:0] Rd, Rs;
  wire [4:0] IMM;
  wire [15:0] adder_3_out, ALU_Result, and_3_out, bit_extender_1_out, Branch_Target_Address, Current_Pc,
       MemOut, multiplexer_1_out, multiplexer_2_out, multiplexer_5_out, or_2_out, PC_q, ReadData1,
       ReadData1_t, ReadData2, subtractor_1_out, X0_q, X1_q, X2_q, X3_q, X4_q, X5_q, X6_q, X7_q;
  wire [15:11] rom_1_data;

  Clock clock_1 (.out(clock_1_out));
  Register #(.width(16)) PC (.D(multiplexer_2_out), .Q(PC_q), .clk(clock_1_out), .clr(in_1));  // open: en
  // Probe on multiplexer_1_out
  // Probe on MemToReg
  Adder #(.width(16)) adder_1 (.a(PC_q), .b(16'h1), .out(Current_Pc));  // open: cin, cout
  // Probe on Branch_Target_Address
  Multiplexer #(.width(16)) multiplexer_1 (
    .in0(ALU_Result), .in1(MemOut), .out(multiplexer_1_out), .sel(MemToReg));  // open: en
  Decoder #(.select(3), .disabled(0)) decoder_1 (
    .out0(decoder_1_out0), .out1(decoder_1_out1), .out2(decoder_1_out2), .out3(decoder_1_out3),
    .out4(decoder_1_out4), .out5(decoder_1_out5), .out6(decoder_1_out6), .out7(decoder_1_out7), .sel(Rd),
    .en(RegWrite));
  // Probe on Rd
  // Probe on Current_Pc
  Multiplexer #(.width(16)) multiplexer_2 (
    .in0(Current_Pc), .in1(Branch_Target_Address), .out(multiplexer_2_out), .sel(or_1_out));  // open: en
  Clock clock_2 (.out(clock_2_out));
  // Probe on Rs
  // Probe on Rd
  ROM #(.addrWidth(16), .dataWidth(16)) rom_1 (.addr(PC_q), .data({rom_1_data, Rd, Rs, IMM}), .sel(1'b1));
  not not_1 (not_1_out, Zero);
  Register #(.width(16)) X0 (.D(multiplexer_1_out), .en(decoder_1_out0), .Q(X0_q), .clk(clock_2_out), .clr(Reset));
  Register #(.width(16)) X1 (.D(multiplexer_1_out), .en(decoder_1_out1), .Q(X1_q), .clk(clock_2_out), .clr(Reset));
  Register #(.width(16)) X2 (.D(multiplexer_1_out), .en(decoder_1_out2), .Q(X2_q), .clk(clock_2_out), .clr(Reset));
  Register #(.width(16)) X3 (.D(multiplexer_1_out), .en(decoder_1_out3), .Q(X3_q), .clk(clock_2_out), .clr(Reset));
  Register #(.width(16)) X4 (.D(multiplexer_1_out), .en(decoder_1_out4), .Q(X4_q), .clk(clock_2_out), .clr(Reset));
  Register #(.width(16)) X5 (.D(multiplexer_1_out), .en(decoder_1_out5), .Q(X5_q), .clk(clock_2_out), .clr(Reset));
  Register #(.width(16)) X6 (.D(multiplexer_1_out), .en(decoder_1_out6), .Q(X6_q), .clk(clock_2_out), .clr(Reset));
  Register #(.width(16)) X7 (.D(multiplexer_1_out), .en(decoder_1_out7), .Q(X7_q), .clk(clock_2_out), .clr(Reset));
  // Probe on IMM
  // Probe on rom_1_data
  and and_1 (and_1_out, BranchEQ, Zero);
  Multiplexer #(.select(3), .width(16)) multiplexer_3 (
    .in0(X0_q), .in1(X1_q), .in2(X2_q), .in3(X3_q), .in4(X4_q), .in5(X5_q), .in6(X6_q), .in7(X7_q),
    .out(ReadData2), .sel(Rd));  // open: en
  and and_2 (and_2_out, BranchNE, not_1_out);
  Multiplexer #(.select(3), .width(16)) multiplexer_4 (
    .in0(X0_q), .in1(X1_q), .in2(X2_q), .in3(X3_q), .in4(X4_q), .in5(X5_q), .in6(X6_q), .in7(X7_q),
    .out(ReadData1_t), .sel(Rs));  // open: en
  // Probe on Rs
  ControlUnit Control_Unit (
    .op0(rom_1_data[11]), .op1(rom_1_data[12]), .op2(rom_1_data[13]), .op3(rom_1_data[14]),
    .op4(rom_1_data[15]), .ALUOp0(ALUOp[0]), .ALUOp1(ALUOp[1]), .ALUSrc(ALUSrc), .RegWrite(RegWrite),
    .MemWrite(MemWrite), .MemRead(MemRead), .MemToReg(MemToReg), .BranchEQ(BranchEQ), .BranchNE(BranchNE));
  or or_1 (or_1_out, and_1_out, and_2_out);
  // Probe on ReadData1_t
  // Probe on ReadData2
  assign bit_extender_1_out = {{11{IMM[4]}}, IMM};  // Bit_Extender bit_extender_1
  // Probe on ALUSrc
  // Probe on ReadData1
  Multiplexer #(.width(16)) multiplexer_5 (
    .in0(ReadData2), .in1(bit_extender_1_out), .out(multiplexer_5_out), .sel(ALUSrc));  // open: en
  // Probe on multiplexer_5_out
  // Probe on Current_Pc
  // Probe on ALU_Result
  Adder #(.width(16)) adder_2 (.a(Current_Pc), .b(bit_extender_1_out), .out(Branch_Target_Address));  // open: cin, cout
  Clock clock_3 (.out(clock_3_out));
  Adder #(.width(16)) adder_3 (.a(ReadData1), .b(multiplexer_5_out), .out(adder_3_out));  // open: cin, cout
  Subtractor #(.width(16)) subtractor_1 (
    .a(ReadData1), .b(multiplexer_5_out), .out(subtractor_1_out));  // open: bin, bout
  assign and_3_out = ReadData1 & multiplexer_5_out;  // AND_Gate and_3, 16 bits wide
  assign or_2_out = ReadData1 | multiplexer_5_out;  // OR_Gate or_2, 16 bits wide
  // Probe on adder_3_out
  // Probe on subtractor_1_out
  // Probe on and_3_out
  // Probe on or_2_out
  RAM #(.addrWidth(16), .dataWidth(16), .bus("separate")) ram_1 (
    .addr(ALU_Result), .din(ReadData2), .data(MemOut), .str(MemWrite), .sel(1'b1), .clk(clock_3_out),
    .ld(MemRead), .clr(1'b0));
  Multiplexer #(.select(2), .width(16)) multiplexer_6 (
    .in0(adder_3_out), .in1(subtractor_1_out), .in2(and_3_out), .in3(or_2_out), .out(ALU_Result), .sel(ALUOp));  // open: en
  // Probe on ALUOp
  // Probe on ALU_Result
  Comparator #(.width(16)) comparator_1 (.a(ALU_Result), .b({16{1'b0}}), .eq(Zero));  // open: gt, lt

  // Notes on the sheet:
  //   WB MUX
  //   Write
  //   PC + 1
  //   PC MUX
  //   PCSrc
  //   Rd  Probe
  //   IMM Probe
  //   Rs Probe
  //   contents of rom_1 (hex, n*v repeats v):
  //   e05 900 a08 b00 8206 2c20 8681 b61 921 2241 8019 4b0a 801f
  //   Opcode
  //   MUX 2
  //   MUX 1
  //   Probe
  //   PC/ FETCH/  DECODE 
  //   Register File
  //   Probe
  //   A Input
  //   ALUSrc MUX
  //   Shifter
  //   Probe
  //   ADD Result
  //   SUB Result
  //   AND Result
  //   OR Result
  //   ALU Result
  //   Probe
  //   ALU
  //   RAM
endmodule

module ControlUnit (
  input  op0,
  input  op1,
  input  op2,
  input  op3,
  input  op4,
  output ALUOp0,
  output ALUOp1,
  output ALUSrc,
  output RegWrite,
  output MemWrite,
  output MemRead,
  output MemToReg,
  output BranchEQ,
  output BranchNE
);

  wire and_1_out, and_2_out, and_3_out, and_4_out, and_6_out, and_7_out, and_8_out, and_9_out, and_10_out,
       not_1_out, not_2_out, not_3_out, not_4_out, not_5_out, not_6_out, not_7_out, not_8_out, not_9_out,
       not_10_out, not_11_out, not_12_out, not_13_out, not_14_out, not_15_out, not_16_out, not_17_out,
       not_18_out, not_19_out, not_20_out, not_21_out, not_22_out, not_23_out, not_24_out, not_25_out,
       not_26_out, not_27_out, not_28_out, not_29_out, not_30_out, not_31_out, not_32_out, not_33_out,
       not_34_out, not_35_out, not_36_out, not_37_out, not_38_out, not_39_out, not_40_out, not_41_out,
       not_42_out, not_43_out, not_44_out, not_45_out, not_46_out, not_47_out, not_48_out, not_49_out,
       not_50_out;

  not not_1 (not_1_out, op0);
  not not_2 (not_2_out, op1);
  not not_3 (not_3_out, op2);
  not not_4 (not_4_out, op3);
  not not_5 (not_5_out, op0);
  not not_6 (not_6_out, op1);
  not not_7 (not_7_out, op2);
  not not_8 (not_8_out, op4);
  not not_9 (not_9_out, op0);
  not not_10 (not_10_out, op1);
  not not_11 (not_11_out, op3);
  not not_12 (not_12_out, op4);
  not not_13 (not_13_out, op2);
  not not_14 (not_14_out, op3);
  not not_15 (not_15_out, op4);
  not not_16 (not_16_out, op2);
  not not_17 (not_17_out, op3);
  not not_18 (not_18_out, op4);
  not not_19 (not_19_out, op1);
  not not_20 (not_20_out, op3);
  not not_21 (not_21_out, op4);
  not not_22 (not_22_out, op2);
  not not_23 (not_23_out, op3);
  not not_24 (not_24_out, op4);
  not not_25 (not_25_out, op1);
  not not_26 (not_26_out, op2);
  not not_27 (not_27_out, op4);
  not not_28 (not_28_out, op1);
  not not_29 (not_29_out, op3);
  not not_30 (not_30_out, op4);
  not not_31 (not_31_out, op2);
  not not_32 (not_32_out, op3);
  not not_33 (not_33_out, op4);
  not not_34 (not_34_out, op1);
  not not_35 (not_35_out, op2);
  not not_36 (not_36_out, op4);
  not not_37 (not_37_out, op1);
  not not_38 (not_38_out, op3);
  not not_39 (not_39_out, op4);
  not not_40 (not_40_out, op1);
  not not_41 (not_41_out, op3);
  not not_42 (not_42_out, op4);
  not not_43 (not_43_out, op0);
  not not_44 (not_44_out, op1);
  not not_45 (not_45_out, op2);
  not not_46 (not_46_out, op3);
  not not_47 (not_47_out, op0);
  not not_48 (not_48_out, op1);
  not not_49 (not_49_out, op2);
  not not_50 (not_50_out, op4);
  and and_1 (and_1_out, not_1_out, not_2_out, not_3_out, not_4_out, op4);
  and and_2 (and_2_out, not_5_out, not_6_out, not_7_out, op3, not_8_out);
  and and_3 (and_3_out, not_9_out, not_10_out, op2, not_11_out, not_12_out);
  and and_4 (and_4_out, op0, op1, not_13_out, not_14_out, not_15_out);
  and and_5 (ALUOp1, op1, not_16_out, not_17_out, not_18_out);
  and and_6 (and_6_out, not_19_out, not_20_out, not_21_out);
  and and_7 (and_7_out, not_22_out, not_23_out, not_24_out);
  and and_8 (and_8_out, op0, not_25_out, not_26_out, not_27_out);
  and and_9 (and_9_out, not_28_out, not_29_out, not_30_out);
  and and_10 (and_10_out, not_31_out, not_32_out, not_33_out);
  and and_11 (MemWrite, op0, not_34_out, not_35_out, op3, not_36_out);
  and and_12 (MemRead, op0, not_37_out, op2, not_38_out, not_39_out);
  and and_13 (MemToReg, op0, not_40_out, op2, not_41_out, not_42_out);
  and and_14 (BranchEQ, not_43_out, not_44_out, not_45_out, not_46_out, op4);
  and and_15 (BranchNE, not_47_out, not_48_out, not_49_out, op3, not_50_out);
  or or_1 (ALUOp0, and_1_out, and_2_out, and_3_out, and_4_out);
  or or_2 (ALUSrc, and_6_out, and_7_out, and_8_out);
  or or_3 (RegWrite, and_9_out, and_10_out);
endmodule
